# Fritzing sketch Steckplan (saved by Fritzing 0.9.6b)
breadboards: 2

parts:
  Part1 = Arduino Nano 33 BLE Sense
  SG1 = Buzzer 12mm [part_number=COM-07950 package=buzzer-12mm-ns]
  LED1 = RGB LED (com. cathode, rgb) [package="5 mm [THT]"]
  R1 = Resistor [tolerance=±5% resistance=220 package="2010 [SMD]"]
  R2 = Resistor [tolerance=±5% resistance=100 package="0603 [SMD]"]
  R3 = Resistor [tolerance=±5% resistance=100 package="0603 [SMD]"]
  S1 = Momentary Switch [package=ksa_sealed_tac_switch]
  S2 = Momentary Switch [package=ksa_sealed_tac_switch]
  R4 = Resistor [tolerance=±5% resistance=10k package="0402 [SMD]"]
  R5 = Resistor [tolerance=±5% resistance=10k package="0402 [SMD]"]
  SW1 = DIP Switch 8 Position [package=dipswitch-08]
  Part2 = Soil Moisture Sensor
  LED2 = smd LED [color="Infrared (880nm)" package="0603 [SMD]"]
  R6 = Resistor [tolerance=±5% resistance=2.2k package="0402 [SMD]"]
  Part3 = Adafruit BME680
  R7 = 8 Resistor Network [part_number=4.7kΩ package="SIP (Single Inline)"]

nets:
  N1: Part1.GND, Part1.A7, SG1.2, LED1.common_cathode
  GND: Part1.D2, S1.3, S2.3, Part2.GND, R6.Pin_1, Part3.GND, R7.9
  N2: Part1.D3~, S1.2
  N3: Part1.D4, S2.2
  N4: Part1.D6~, SW1.8, R7.8
  N5: Part1.D7, SW1.7, R7.7
  N6: Part1.D8, SW1.6, R7.6
  N7: Part1.D9~, SW1.5, R7.5
  N8: Part1.D10~, SW1.4, R7.4
  N9: Part1.D11/MOSI, Part1.+5V, SW1.3, R7.3
  N10: Part1.D12~/MISO, SW1.2, R7.2
  N11: Part1.A6, LED2.anode, R6.Pin_0
  N12: Part1.A5, Part2.SIG
  N13: Part1.A4, Part3.SDI/SDA
  N14: Part1.A3, Part3.SCK/SCL
  N15: Part1.A2, R2.Pin_1
  N16: Part1.A1, R3.Pin_1
  N17: Part1.A0, R1.Pin_1
  N18: Part1.AREF, SG1.1
  N19: LED1.red_anode, R1.Pin_0
  N20: LED1.green_anode, R3.Pin_0
  N21: LED1.blue_anode, R2.Pin_0
  N22: S1.1, R5.Pin_0
  VCC: R4.Pin_0, R5.Pin_1, SW1.9, SW1.10, SW1.11, SW1.12, SW1.13, SW1.14, SW1.15, SW1.16, Part2.VCC, LED2.cathode, Part3.VIN
  N23: SW1.1, R7.1

custom parts:
  Arduino Nano 33 BLE Sense: The Nano 33 BLE Sense (without headers) is Arduino’s 3.3V AI enabled board in the smallest available form factor: 45x18mm! The Arduino Nano 33 BLE Sense is a completely new board on a well-known form factor. It comes with a series of embedded sensors: 9 axis inertial sensor: what makes this board ideal for wearable devices humidity, and temperature sensor: to get highly accurate measurements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
  Buzzer 12mm: Buzzer 12mm Spark Fun Electronics SKU : Comp-Buzzer Through hole This is a small 12mm round speaker that operates around the audible 2kHz range. You can use these speakers to create simple music or user interfaces. This is not a true piezoelectric speaker but behaves similarly. Instead of a piezoelectric crystal that vibrates with an electric current, this tiny speaker uses an electromagnet to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
